# Fritzing sketch BaseSensor (saved by Fritzing 0.9.10b)

parts:
  Part1 = Adafruit Feather M0 RFM69 [part_number="Adafruit #3176 or #3177"]
  ANT1 = Antenna
  Mod1 = KY-004 Key Switch Module [package="Breakout board"]

nets:
  N1: Part1.GND, Mod1.-
  +3V3: Part1.+3V3, Mod1.Vin
  N2: Part1.ANT, ANT1.antenna_lead
  N3: Part1.D13, Mod1.S

custom parts:
  Adafruit Feather M0 RFM69: This is the Adafruit Feather M0 RFM69 Packet Radio - our take on an microcontroller with a RFM69HCW packet radio transceiver plus built in USB and battery charging. Its an Adafruit Feather M0 with a 433MHz or 900MHz radio module cooked in! We have other boards in the Feather family, check'em out here. At the Feather M0's heart is an ATSAMD21G18 ARM Cortex M0 processor, clocked at 48 MHz and at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
  KY-004 Key Switch Module: Arduino Key Switch Module Keyes KY-004 is a push button that will output a high signal when pressed.
